# Fritzing sketch led_matrix_metronome (saved by Fritzing 0.9.4)
breadboards: 1

parts:
  Part1 = Arduino Uno (Rev3)
  SG1 = Buzzer 12mm [package=buzzer-12mm-ns]
  R1 = Rotary Potentiometer (Small) [maximum_resistance=100kΩ package=THT]
  S2 = Momentary Switch [package=ksa_sealed_tac_switch]
  R2 = Resistor [tolerance=±5% resistance=10k package=THT]
  Part2 = Bicolor 8x8 LED Matrix Backpack [part_number=902]

nets:
  N1: Part1.A0, R1.wiper
  N2: Part1.A4/SDA, Part2.SDA
  N3: Part1.A5/SCL, Part2.SCL
  N4: Part1.D8, SG1.1
  N5: Part1.D2, S2.2, R2.Pin_0
  5V: Part1.5V, R1.leg1, S2.4, Part2.VDD
  GND: Part1.GND, SG1.2, R1.leg2, R2.Pin_1, Part2.GND

custom parts:
  Bicolor 8x8 LED Matrix Backpack: This 1.2" bi-color 8x8 LED matrix includes a driver chip for simple control via an I2C interface. It's called a Bicolor LED, but you can have 3 colors total by turning on the red and green LEDs, which creates yellow. That's 3 colors for the price of 2! The backpacks come with address-selection jumpers so you can connect up to eight bicolor matrices on a single I2C bus.
